// Logisim project 16x4_mux.circ as structural Verilog: 1 circuit, main circuit 16x4_mux
module _16x4_mux (
  input  S1,
  input  S0,
  input  A3,
  input  A2,
  input  A1,
  input  A0,
  input  B3,
  input  B2,
  input  B1,
  input  B0,
  input  C3,
  input  C2,
  input  C1,
  input  C0,
  input  D3,
  input  D2,
  input  D1,
  input  D0,
  output O3,
  output O2,
  output O1,
  output O0
);

  wire and_1_out, and_2_out, and_3_out, and_4_out, and_5_out, and_6_out, and_7_out, and_8_out, and_9_out,
       and_10_out, and_11_out, and_12_out, and_13_out, and_14_out, and_15_out, and_16_out, not_1_out,
       not_2_out, not_3_out, not_4_out, not_5_out, not_6_out, not_7_out, not_8_out, not_9_out, not_10_out,
       not_11_out, not_12_out, not_13_out, not_14_out, not_15_out, not_16_out, or_1_out, or_2_out, or_3_out,
       or_4_out;

  not not_1 (not_1_out, S1);
  not not_2 (not_2_out, S0);
  not not_3 (not_3_out, S1);
  not not_4 (not_4_out, S0);
  not not_5 (not_5_out, S1);
  not not_6 (not_6_out, S0);
  not not_7 (not_7_out, S1);
  not not_8 (not_8_out, S0);
  not not_9 (not_9_out, S1);
  not not_10 (not_10_out, S0);
  not not_11 (not_11_out, S1);
  not not_12 (not_12_out, S0);
  not not_13 (not_13_out, S1);
  not not_14 (not_14_out, S0);
  not not_15 (not_15_out, S1);
  not not_16 (not_16_out, S0);
  and and_1 (and_1_out, not_1_out, not_2_out, A3);
  and and_2 (and_2_out, not_3_out, S0, B3);
  and and_3 (and_3_out, S1, not_4_out, C3);
  and and_4 (and_4_out, S1, S0, D3);
  and and_5 (and_5_out, not_5_out, not_6_out, A2);
  and and_6 (and_6_out, not_7_out, S0, B2);
  and and_7 (and_7_out, S1, not_8_out, C2);
  and and_8 (and_8_out, S1, S0, D2);
  and and_9 (and_9_out, not_9_out, not_10_out, A1);
  and and_10 (and_10_out, not_11_out, S0, B1);
  and and_11 (and_11_out, S1, not_12_out, C1);
  and and_12 (and_12_out, S1, S0, D1);
  and and_13 (and_13_out, not_13_out, not_14_out, A0);
  and and_14 (and_14_out, not_15_out, S0, B0);
  and and_15 (and_15_out, S1, not_16_out, C0);
  and and_16 (and_16_out, S1, S0, D0);
  or or_1 (or_1_out, and_1_out, and_2_out, and_3_out, and_4_out);
  or or_2 (or_2_out, and_5_out, and_6_out, and_7_out, and_8_out);
  or or_3 (or_3_out, and_9_out, and_10_out, and_11_out, and_12_out);
  or or_4 (or_4_out, and_13_out, and_14_out, and_15_out, and_16_out);
endmodule
